# Fritzing sketch Arduino LED Dimmer (saved by Fritzing 0.9.1b)
breadboards: 1

parts:
  R1 = Rotary Potentiometer (Small) [maximum_resistance=100kΩ package=THT]
  LED1 = LEDs [package=led10mm]
  R2 = Resistor [tolerance=±5% resistance=220 package="0805 [SMD]"]
  Part1 = Arduino Uno (Rev3)

nets:
  N1: R1.leg2, Part1.3V3
  N2: LED1.A, Part1.GND
  N3: LED1.C, R2.Pin_0
  N4: R2.Pin_1, Part1.D3_PWM
